# Fritzing sketch 2-ControllingVolume (saved by Fritzing 0.9.1b)
breadboards: 1

parts:
  U1 = 74HC04_HEX_INVERTER [package=dil14]
  VCC1 = Battery block 9V
  C1 = Ceramic Capacitor [capacitance=100nF package="100 mil [THT, multilayer]"]
  C2 = Capacitor Polarized [package=cpol-radial-10uf-25v]
  R2 = Resistor [tolerance=±5% resistance=10k package=THT]
  R3 = Resistor [tolerance=±5% resistance=1k package=THT]
  R4 = Photocell (LDR) [package=THT]

nets:
  N1: U1.1A, C1.1, R4.pin_0
  N2: U1.1Y, C2.-, R4.pin_1
  N3: U1.GND, VCC1.-, C1.0, R3.Pin_0
  N4: U1.VCC, VCC1.+
  N5: C2.+, R2.Pin_0
  N6: R2.Pin_1, R3.Pin_1
