# Fritzing sketch 4-MixingTwoOscillators (saved by Fritzing 0.9.1b)
circuit board: 2.84581cm x 4.19748cm
breadboards: 1

parts:
  VCC1 = Battery block 9V
  C2 = Capacitor Polarized [package=cpol-radial-10uf-25v]
  R2 = Resistor [tolerance=±5% resistance=10k package=THT]
  R3 = Resistor [tolerance=±5% resistance=1k package=THT]
  R4 = Photocell (LDR) [package=THT]
  U2 = CD40106 [package=dil14]
  TRS1 = Audio Jack (TRS) 3.5mm [package="4Ucon 08780 [THT]"]
  C1 = Ceramic Capacitor [capacitance=100nF package="100 mil [THT, multilayer]"]
  C3 = Ceramic Capacitor [capacitance=100nF package="100 mil [THT, multilayer]"]
  R5 = Rotary Potentiometer (Small) [maximum_resistance=100kΩ package=THT]
  R6 = Resistor [tolerance=±5% resistance=10k package=THT]
  R7 = Resistor [tolerance=±5% resistance=10k package=THT]

nets (from the breadboard view):
  N1: VCC1.-, R3.Pin_0, U2.GND, TRS1.Sleeve, C1.0, C3.0
  N2: VCC1.+, U2.VCC
  N3: C2.+, R2.Pin_0
  N4: C2.-, R6.Pin_1, R7.Pin_1
  N5: R2.Pin_1, R3.Pin_1, TRS1.Tip
  N6: R4.pin_0, U2.1A, C1.1
  N7: R4.pin_1, U2.1Y, R7.Pin_0
  N8: U2.2A, C3.1, R5.wiper
  N9: U2.2Y, R5.leg1, R6.Pin_0
