# Fritzing sketch 5-NANDSynth (saved by Fritzing 0.9.1b)
circuit board: 2.84581cm x 4.19748cm
breadboards: 1

parts:
  VCC1 = Battery block 9V
  C2 = Capacitor Polarized [package=cpol-radial-10uf-25v]
  R2 = Resistor [tolerance=±5% resistance=10k package=THT]
  R3 = Resistor [tolerance=±5% resistance=1k package=THT]
  R4 = Photocell (LDR) [package=THT]
  TRS1 = Audio Jack (TRS) 3.5mm [package="4Ucon 08780 [THT]"]
  C1 = Ceramic Capacitor [capacitance=100nF package="100 mil [THT, multilayer]"]
  U1 = CD4093 [package="DIP14 [THT]"]

nets:
  N1: VCC1.-, R3.Pin_0, TRS1.Sleeve, C1.0, U1.GND
  N2: VCC1.+, U1.1A, U1.VCC
  N3: C2.+, R2.Pin_0
  N4: C2.-, R4.pin_1, U1.NC#2
  N5: R2.Pin_1, R3.Pin_1, TRS1.Tip
  N6: R4.pin_0, C1.1, U1.1B

custom parts:
  CD4093: Dual 4-Input Positive-NAND Gates
