# Fritzing sketch circuit-example (saved by Fritzing 0.9.1b)
breadboards: 1

parts:
  Battery = Battery block 9V
  LED1 = smd LED [color="Red (633nm)" package="1206 [SMD]"]
  R1 = Resistor [tolerance=±5% resistance=470 package=THT]

nets:
  N1: Battery.-, LED1.cathode
  N2: Battery.+, R1.Pin_0
  N3: LED1.anode, R1.Pin_1
