# Fritzing sketch passive-mixer (saved by Fritzing 0.9.1b)
circuit board: 8.46667cm x 5.64444cm
breadboards: 1

parts:
  Out = Audio Jack (TRS) 3.5mm [package="4Ucon 08780 [THT]"]
  In_3 = Audio Jack (TRS) 3.5mm [package="4Ucon 08780 [THT]"]
  In_2 = Audio Jack (TRS) 3.5mm [package="4Ucon 08780 [THT]"]
  In_1 = Audio Jack (TRS) 3.5mm [package="4Ucon 08780 [THT]"]
  R1 = Resistor [tolerance=±5% resistance=10k package=THT]
  R3 = Resistor [tolerance=±5% resistance=10k package=THT]
  R2 = Resistor [tolerance=±5% resistance=10k package=THT]

nets:
  N1: Out.Sleeve, In_3.Sleeve, In_2.Sleeve, In_1.Sleeve
  N2: Out.Tip, In_1.Tip, R1.Pin_0, R1.Pin_1, R3.Pin_0, R2.Pin_0
  N3: In_3.Tip, R2.Pin_1
  N4: In_2.Tip, R3.Pin_1
